# Fritzing sketch triggerbox (saved by Fritzing 0.9.3b)
perfboards: 1

parts:
  Bauteil1 = Arduino Leonardo (Rev3b)
  S1 = Pushbutton [package="[THT]"]
  S2 = Toggle Switch [package=THT]
  RE1 = Rotary Encoder [package=THT]
  R1 = Resistor [tolerance=±5% resistance=10k package=THT]
  S3 = Square Pushbutton
  S5 = SWITCH-SP3T [package=switch-sp3t-smd]
  J1 = Power Jack [package=power_jack_smd]
  U1 = RELAY-SOLIDSTATE [package=relay-s108t02]
  LED2 = LED - 5mm [color="Blue (505nm)" package="5 mm [THT]"]
  VCC1 = Battery
  VCC2 = Battery
  J2 = Power Jack [package=power_jack_smd]
  LED3 = LED - 5mm [color="Blue (505nm)" package="5 mm [THT]"]
  R2 = Rotary Potentiometer (Small) [maximum_resistance=50kΩ package=THT]  # not connected
  U2 = 7-SEGMENT-4DIGIT [package=7-segment-4digit]  # not connected
  Power_plug1 = Power plug
  JP1 = Header 2 [package=r_sw_th]
  R3 = Resistor [tolerance=±5% resistance=100 package=THT]  # not connected
  U3 = MAGJACK-POE [package=magjack-poe]

nets:
  N1: Bauteil1.D0/RX, U3.RCT
  N2: Bauteil1.D1/TX, U3.RD-
  N3: Bauteil1.D2/SDA, S1.Pin_1, S1.Pin_2, J1.GND
  N4: Bauteil1.D3_PWM/SCL, S5.4
  N5: Bauteil1.D4/A6, S2.L1
  N6: Bauteil1.3V3, U3.SHIELD
  N7: Bauteil1.GND, S1.Pin_4, S5.3, J1.GNDBREAK, U1.-, VCC2.-
  N8: Bauteil1.VIN, VCC2.+
  N9: Bauteil1.A0, U3.TCT
  N10: Bauteil1.A1, U3.TD+
  N11: Bauteil1.A3, RE1.EncoderPinB
  N12: Bauteil1.A4, RE1.EncoderPinA
  N13: Bauteil1.A5, R1.Pin_0
  N14: Bauteil1.D13_PWM, LED2.anode
  N15: S2.COM, U1.+, LED3.anode
  N16: S3.leg1, J1.PWR
  N17: S5.1, VCC1.+
  N18: U1.T2, J2.GND
  N19: Power_plug1.VCC, JP1.1

notes:
  GND
  VIN
  3V
  CLK
  MOSI
  CS
  MISO
  LITE
  w/MicroSD Socket - HXD8357D
  VCC
  SCK
  RESET
  SPI MODE !
  3.5" TFT 320x480 + Touchscreen Breakout Board
  IM2
  D/C
  RST
  Y+
  X+
  Y-
  X-
  IM1
  IM0
  CCS
  CD
  Trigger:
  Trigger: Wire remote
  Barrel jack or Chinch
  Rotary encoder with push btn
  10KOhm
  On board
  Triggered?
  POWER SUPPLY 5V 5amp
  POWER SUPPLY 30V 8amp
  solid state
  OPEN RELAY LED
  #3
  #4
  #2
  #5
  #6
  DPDT On-On
  SAFETY: DISABLE ALL RELAYS
  Voltmeter 0-100V
  50K Poti: External Voltage adj.
  DC/DC power converter
  OUT: 0-±29V
  IN: 30V
  3.0-10V
  0-60V
  Connector #1: for trigger device #1
  - - - - - - - - - - - - - - - - - - - - - - - - - - - - - - - - - - - - - - - - - - - - - - - - - - - - - - - - - - - - - - - - - - - - - - - -
  - - - - - - - - - - - - - - - - - - - - - - - - - - - - - - - - - - - - - - - - - - - - -
  REPEAT 6x
  OVERRIDE
  MANUAL
  METRO M0
  - - - - - - - - - - - - - - -
  EXPRESS
  (Double pole, double throw)
  230V AC
  240V ROCKER
  #1
  RELAY 5amp
  100 Ohm
  RJ45: External
  sensor connection
  Signal LED:
